# Fritzing sketch Auto con Leds Placav2 (saved by Fritzing 0.8.3b)
breadboards: 1

parts:
  Bateria_9V = BC9VPC [package=bc9vpc]
  Puente_H_L293D = L293D [part_number="Puente H L293D" package=THT]
  Motor_Traccion = DC Motor
  Motor_Giro = DC Motor [part_number="Motor Giro"]
  GY-521_Acelerometro = MPU-6050 Board GY-521 [form="♀ (female)" part_number="GY-521 Acelerometro" package=THT]
  R2 = Resistor [tolerance=±5% resistance=220 package=THT]
  R3 = Resistor [tolerance=±5% resistance=220 package=THT]
  R1 = Resistor [tolerance=±5% resistance=220 package=THT]
  U1 = Voltage Regulator - 5V [package="TO220 [THT]"]  # not connected
  HC-SR04_Proximidad_Delantero = SRF05 Ultrasonic Rangefinder
  HC-SR04_Proximidad_Trasero = SRF05 Ultrasonic Rangefinder
  HC-05_Bluetooth = Bluetooth HC-05 Macho
  Led_Delantero_2 = LED - 3mm [color="White (6500K)" package="3 mm [THT]"]
  Led_Delantero_1 = LED - 3mm [color="White (6500K)" package="3 mm [THT]"]
  Led_Marcha_Atras_1 = LED - 3mm [color="White (6500K)" package="3 mm [THT]"]
  Led_Marcha_Atras_2 = LED - 3mm [color="White (6500K)" package="3 mm [THT]"]
  Led_Encendido1 = LED - 3mm [color="Red (660nm)" package="3 mm [THT]"]
  Led_Encendido = LED - 3mm [color="Red (660nm)" package="3 mm [THT]"]
  Arduino_UNO = Arduino Uno (Rev3)

nets (from the schematic view):
  GND: Bateria_9V.V+, Puente_H_L293D.0V, GY-521_Acelerometro.pin2, HC-SR04_Proximidad_Delantero.GND, HC-SR04_Proximidad_Trasero.GND, HC-05_Bluetooth.GND, Led_Delantero_2.anode, Led_Delantero_1.anode, Led_Marcha_Atras_1.anode, Led_Marcha_Atras_2.anode, Led_Encendido1.anode, Led_Encendido.anode
  VCC: Bateria_9V.V-, Puente_H_L293D.+Vmotor, HC-SR04_Proximidad_Delantero.VCC, HC-SR04_Proximidad_Trasero.VCC, HC-05_Bluetooth.VCC, Arduino_UNO.VIN
  N1: Puente_H_L293D.Enable_1, Puente_H_L293D.Enable_2, GY-521_Acelerometro.pin1, Arduino_UNO.5V
  N2: Puente_H_L293D.In_1, Arduino_UNO.D10_PWM/SS
  N3: Puente_H_L293D.Out_1_(_Controlled_by_Enable_1_), Motor_Traccion.pin_2
  N4: Puente_H_L293D.Out_2_(_Controlled_by_Enable_1_), Motor_Traccion.pin_1
  N5: Puente_H_L293D.In_2, Arduino_UNO.D9_PWM
  N6: Puente_H_L293D.In_3, Arduino_UNO.D5_PWM
  N7: Puente_H_L293D.Out_3_(_Controlled_by_Enable_2_), Motor_Giro.pin_2
  N8: Puente_H_L293D.Out_4_(_Controlled_by_Enable_2_), Motor_Giro.pin_1
  N9: Puente_H_L293D.In_4, Arduino_UNO.D6_PWM
  N10: GY-521_Acelerometro.pin3, Arduino_UNO.A5/SCL
  N11: GY-521_Acelerometro.pin4, Arduino_UNO.A4/SDA
  N12: GY-521_Acelerometro.pin8, Arduino_UNO.D4
  N13: R2.Pin_0, Led_Delantero_2.cathode, Led_Delantero_1.cathode
  N14: R2.Pin_1, Arduino_UNO.D8
  N15: R3.Pin_0, Led_Encendido1.cathode, Led_Encendido.cathode
  N16: R1.Pin_0, Led_Marcha_Atras_1.cathode, Led_Marcha_Atras_2.cathode
  N17: R1.Pin_1, Arduino_UNO.D7
  N18: HC-SR04_Proximidad_Delantero.Echo, Arduino_UNO.D2
  N19: HC-SR04_Proximidad_Trasero.Trig, Arduino_UNO.D11_PWM/MOSI
  N20: HC-SR04_Proximidad_Trasero.Echo, Arduino_UNO.D12/MISO
  N21: HC-05_Bluetooth.TXD, Arduino_UNO.D0/RX
  N22: HC-05_Bluetooth.RXD, Arduino_UNO.D1/TX
  N23: Arduino_UNO.ICSP_SCK, Arduino_UNO.D13/SCK

custom parts:
  MPU-6050 Board GY-521: Acelerometro y Giroscopio MPU-6050 Board GY-521
