# Fritzing sketch Auto con Leds Placav5 (saved by Fritzing 0.8.3b)
circuit board: 9.1cm x 7.1cm
breadboards: 1

parts:
  Arduino_UNO = Arduino Uno (Rev3)
  Bateria_9V = BC9VPC [package=bc9vpc]
  Puente_H_L293D = L293D [part_number="Puente H L293D" package=THT]
  Motor_Traccion = DC Motor
  Motor_Giro = DC Motor [part_number="Motor Giro"]
  GY-521_Acelerometro = MPU-6050 Board GY-521 [form="♀ (female)" part_number="GY-521 Acelerometro" package=THT]
  R2 = Resistor [tolerance=±5% resistance=220 package=THT]
  R3 = Resistor [tolerance=±5% resistance=220 package=THT]
  R1 = Resistor [tolerance=±5% resistance=220 package=THT]
  7805 = Voltage Regulator - 5V [package="TO220 [THT]"]
  Led_Delantero_2 = LED - 3mm [color="White (6500K)" package="3 mm [THT]"]
  Led_Delantero_1 = LED - 3mm [color="White (6500K)" package="3 mm [THT]"]
  Led_Marcha_Atras_2 = LED - 3mm [color="White (6500K)" package="3 mm [THT]"]
  Led_Marcha_Atras_1 = LED - 3mm [color="White (6500K)" package="3 mm [THT]"]
  Led_Encendido1 = LED - 3mm [color="Red (660nm)" package="3 mm [THT]"]
  Led_Encendido_2 = LED - 3mm [color="Red (660nm)" package="3 mm [THT]"]
  HC-SR04_Proximidad_Delantero = SRF05 Ultrasonic Rangefinder
  HC-SR04_Proximidad_Trasero = SRF05 Ultrasonic Rangefinder
  HC-05_Bluetooth = Bluetooth HC-05 Macho

nets:
  N1: Arduino_UNO.A4/SDA, GY-521_Acelerometro.pin4
  N2: Arduino_UNO.A5/SCL, GY-521_Acelerometro.pin3
  N3: Arduino_UNO.ICSP_SCK, Arduino_UNO.D13/SCK, R3.Pin_1
  GND: Arduino_UNO.GND, Bateria_9V.V+, Puente_H_L293D.0V, GY-521_Acelerometro.pin2, GY-521_Acelerometro.pin7, 7805.GND, Led_Delantero_2.anode, Led_Delantero_1.anode, Led_Marcha_Atras_2.anode, Led_Marcha_Atras_1.anode, Led_Encendido1.anode, Led_Encendido_2.anode, HC-SR04_Proximidad_Delantero.GND, HC-SR04_Proximidad_Trasero.GND, HC-05_Bluetooth.GND
  N4: Arduino_UNO.D8, R2.Pin_1
  N5: Arduino_UNO.D9_PWM, Puente_H_L293D.In_2
  N6: Arduino_UNO.D10_PWM/SS, Puente_H_L293D.In_1
  N7: Arduino_UNO.D11_PWM/MOSI, HC-SR04_Proximidad_Trasero.Trig
  N8: Arduino_UNO.D12/MISO, HC-SR04_Proximidad_Trasero.Echo
  N9: Arduino_UNO.D0/RX, HC-05_Bluetooth.TXD
  N10: Arduino_UNO.D1/TX, HC-05_Bluetooth.RXD
  N11: Arduino_UNO.D2, HC-SR04_Proximidad_Delantero.Echo
  N12: Arduino_UNO.D3_PWM, HC-SR04_Proximidad_Delantero.Trig
  N13: Arduino_UNO.D4, GY-521_Acelerometro.pin8
  N14: Arduino_UNO.D5_PWM, Puente_H_L293D.In_3
  N15: Arduino_UNO.D6_PWM, Puente_H_L293D.In_4
  N16: Arduino_UNO.D7, R1.Pin_1
  N17: Arduino_UNO.5V, Puente_H_L293D.Enable_1, Puente_H_L293D.Enable_2, GY-521_Acelerometro.pin1
  VCC: Arduino_UNO.VIN, Bateria_9V.V-, Puente_H_L293D.+Vmotor, 7805.input_voltage, 7805.output_voltage, HC-SR04_Proximidad_Delantero.VCC, HC-SR04_Proximidad_Trasero.VCC, HC-05_Bluetooth.VCC
  N18: Puente_H_L293D.Out_1_(_Controlled_by_Enable_1_), Motor_Traccion.pin_2
  N19: Puente_H_L293D.Out_2_(_Controlled_by_Enable_1_), Motor_Traccion.pin_1
  N20: Puente_H_L293D.Out_3_(_Controlled_by_Enable_2_), Motor_Giro.pin_2
  N21: Puente_H_L293D.Out_4_(_Controlled_by_Enable_2_), Motor_Giro.pin_1
  N22: R2.Pin_0, Led_Delantero_2.cathode, Led_Delantero_1.cathode
  N23: R3.Pin_0, Led_Encendido1.cathode, Led_Encendido_2.cathode
  N24: R1.Pin_0, Led_Marcha_Atras_2.cathode, Led_Marcha_Atras_1.cathode

custom parts:
  MPU-6050 Board GY-521: Acelerometro y Giroscopio MPU-6050 Board GY-521
