# Fritzing sketch Auto con Leds Placav7 (saved by Fritzing 0.8.3b)
circuit board: 10cm x 6cm
breadboards: 1

parts:
  Arduino_UNO = Arduino Uno (Rev3)
  Puente_H_L293D = L293D [part_number="Puente H L293D" package=THT]
  Motor_Traccion = DC Motor
  Motor_Giro = DC Motor [part_number="Motor Giro"]
  GY-521_Acelerometro = MPU-6050 Board GY-521 [form="♀ (female)" part_number="GY-521 Acelerometro" package=THT]
  R2 = Resistor [tolerance=±5% resistance=220 package=THT]
  R3 = Resistor [tolerance=±5% resistance=220 package=THT]
  R1 = Resistor [tolerance=±5% resistance=220 package=THT]
  7805 = Voltage Regulator - 5V [package="TO220 [THT]"]
  Led_Delantero_2 = LED - 3mm [color="White (6500K)" package="3 mm [THT]"]
  Led_Delantero_1 = LED - 3mm [color="White (6500K)" package="3 mm [THT]"]
  Led_Marcha_Atras_2 = LED - 3mm [color="White (6500K)" package="3 mm [THT]"]
  Led_Marcha_Atras_1 = LED - 3mm [color="White (6500K)" package="3 mm [THT]"]
  Led_Encendido1 = LED - 3mm [color="Red (660nm)" package="3 mm [THT]"]
  Led_Encendido_2 = LED - 3mm [color="Red (660nm)" package="3 mm [THT]"]
  Sensor_Trasero = HC-SR04
  Sensor_Delantero = HC-SR04
  VCC1 = Battery block 9V
  HC-05_Bluetooth = Bluetooth HC-05 Macho

nets:
  N1: Arduino_UNO.A4/SDA, GY-521_Acelerometro.pin4
  N2: Arduino_UNO.A5/SCL, GY-521_Acelerometro.pin3
  N3: Arduino_UNO.ICSP_MISO, Arduino_UNO.D12/MISO, Sensor_Trasero.Echo
  N4: Arduino_UNO.ICSP_SCK, Arduino_UNO.D13/SCK, R3.Pin_1
  N5: Arduino_UNO.ICSP_MOSI, Arduino_UNO.D11_PWM/MOSI, Sensor_Trasero.Trig
  GND: Arduino_UNO.GND, Puente_H_L293D.0V, GY-521_Acelerometro.pin2, GY-521_Acelerometro.pin7, 7805.GND, Led_Delantero_2.anode, Led_Delantero_1.anode, Led_Marcha_Atras_2.anode, Led_Marcha_Atras_1.anode, Led_Encendido1.anode, Led_Encendido_2.anode, Sensor_Trasero.GND, Sensor_Delantero.GND, VCC1.-, HC-05_Bluetooth.GND
  N6: Arduino_UNO.D8, R2.Pin_1
  N7: Arduino_UNO.D9_PWM, Puente_H_L293D.In_2
  N8: Arduino_UNO.D10_PWM/SS, Puente_H_L293D.In_1
  N9: Arduino_UNO.D0/RX, HC-05_Bluetooth.TXD
  N10: Arduino_UNO.D1/TX, HC-05_Bluetooth.RXD
  N11: Arduino_UNO.D2, Sensor_Delantero.Echo
  N12: Arduino_UNO.D3_PWM, Sensor_Delantero.Trig
  N13: Arduino_UNO.D4, GY-521_Acelerometro.pin8
  N14: Arduino_UNO.D5_PWM, Puente_H_L293D.In_3
  N15: Arduino_UNO.D6_PWM, Puente_H_L293D.In_4
  N16: Arduino_UNO.D7, R1.Pin_1
  VCC: Arduino_UNO.5V, Arduino_UNO.VIN, Puente_H_L293D.Enable_1, Puente_H_L293D.+Vmotor, Puente_H_L293D.Enable_2, GY-521_Acelerometro.pin1, 7805.input_voltage, Sensor_Trasero.VCC, Sensor_Delantero.VCC, VCC1.+
  N17: Puente_H_L293D.Out_1_(_Controlled_by_Enable_1_), Motor_Traccion.pin_2
  N18: Puente_H_L293D.Out_2_(_Controlled_by_Enable_1_), Motor_Traccion.pin_1
  N19: Puente_H_L293D.Out_3_(_Controlled_by_Enable_2_), Motor_Giro.pin_2
  N20: Puente_H_L293D.Out_4_(_Controlled_by_Enable_2_), Motor_Giro.pin_1
  N21: R2.Pin_0, Led_Delantero_2.cathode, Led_Delantero_1.cathode
  N22: R3.Pin_0, Led_Encendido1.cathode, Led_Encendido_2.cathode
  N23: R1.Pin_0, Led_Marcha_Atras_2.cathode, Led_Marcha_Atras_1.cathode
  N24: 7805.output_voltage, HC-05_Bluetooth.VCC

custom parts:
  MPU-6050 Board GY-521: Acelerometro y Giroscopio MPU-6050 Board GY-521
